# Fritzing sketch ProtoStaxAG_WeatherStation (saved by Fritzing 1.0.5)

parts:
  A1 = Arduino GIGA R1 WiFi
  Part1 = Adafruit BME280

nets:
  N1: A1.Pin_27, A1.Pin_64, Part1.VIN
  N2: A1.Pin_30, A1.Pin_106, Part1.GND
  N3: A1.Pin_140, Part1.SCK/SCL
  N4: A1.Pin_141, Part1.SDI/SDA

custom parts:
  Arduino GIGA R1 WiFi: The Arduino GIGA R1 WiFi is designed for ambitious makers who want to step up their game.
  Adafruit BME280: Bosch has stepped up their game with their new BME280 sensor, an environmental sensor with temperature, barometric pressure and humidity! This sensor is great for all sorts of weather/environmental sensing and can even be used in both I2C and SPI! This precision sensor from Bosch is the best low-cost sensing solution for measuring humidity with ±3% accuracy, barometric pressure with ±1 hPa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
